# Fritzing sketch Lab7 (saved by Fritzing 0.9.3b)
breadboards: 1

parts:
  Part1 = SparkFun ESP8266 Thing
  LED1 = LED - 5mm [color="Red (633nm)" package="5 mm [THT]"]  # not connected
  R1 = Resistor [tolerance=±5% resistance=330 package=THT]
  LED2 = LED - 5mm [color="Red (633nm)" package="5 mm [THT]"]  # not connected
  R2 = Resistor [tolerance=±5% resistance=330 package=THT]
  Grove1 = Grove OLED 128x96  # not connected
  RHT1 = Humidity and Temperature Sensor RHT03
  J1 = Infrared Proximity Sensor

nets:
  GND: Part1.GND, R1.Pin_0, R2.Pin_0, RHT1.GND_2, J1.GND
  VCC: Part1.VCC, RHT1.Vcc
  N1: Part1.USBVCC, J1.Vcc
  N2: Part1.GPIO13, J1.Vout
  N3: Part1.GPIO12, RHT1.Data-signal

notes:
  Your motion sensor
  does not look like this
